# Fritzing sketch SensorWebEnergy (saved by Fritzing 0.8.3b)
breadboards: 1

parts:
  Componente1 = Arduino Uno (Rev3)
  RHT1 = Humidity and Temperature Sensor RHT03
  T1 = LM35 Temperature Sensor [package="TO92 [THT]"]
  T2 = LM35 Temperature Sensor [package="TO92 [THT]"]
  S1 = Reed switch [package=THT]
  S2 = Reed switch [package=THT]
  S3 = Reed switch [package=THT]
  U1 = mystery part, 3 pins [chip_label=?]
  U2 = mystery part, 3 pins [chip_label=?]
  R1 = Resistor [tolerance=±5% resistance=10k package=THT]
  R2 = Resistor [tolerance=±5% resistance=10k package=THT]
  R3 = Resistor [tolerance=±5% resistance=10k package=THT]
  R5 = Resistor [tolerance=±5% resistance=4.7k package=THT]
  R6 = Resistor [tolerance=±5% resistance=4.7k package=THT]

nets:
  N1: Componente1.A1, U2.pin1
  N2: Componente1.A2, U1.pin1
  N3: Componente1.A3, RHT1.Data-signal
  N4: Componente1.D10_PWM/SS, R3.Pin_1
  N5: Componente1.D3_PWM, R2.Pin_1
  N6: Componente1.D4, R1.Pin_1
  N7: Componente1.D5_PWM, T2.Vout, R5.Pin_1
  N8: Componente1.D6_PWM, T1.Vout, R6.Pin_1
  N9: RHT1.Vcc, T1.+Vs, T2.+Vs, U1.pin2, U2.pin2, R5.Pin_0, R6.Pin_0
  GND: RHT1.GND_1, RHT1.GND_2, T1.GND, T2.GND, U1.pin3, U2.pin3
  N10: S1.pin_1, S2.pin_1, S3.pin_1, R1.Pin_0, R2.Pin_0, R3.Pin_0
  N11: S1.pin_2, S2.pin_2, S3.pin_2

notes:
  DHT22
  DS18B20
  SONAR
  CT
  ASH
  BOILER
  FLOW
  3 Resistor of 10Kohm
  2 Resistor of 4.7Kohm
